# Fritzing sketch ConstantCurrent_DummyLoad (saved by Fritzing 0.9.3b)
breadboards: 2

parts:
  U1 = LM124-324 Quad Opamp [part_number=LM324 package="DIP (Dual Inline)"]
  RV2 = TRIMPOT [part_number=10K package=trimpot_pth_s3_lock]
  F1 = Fan - Ventilador [package=THT]
  Part1 = LCD1602-I2C
  Part2 = Arduino Nano (Rev3.0) (ICSP) [part_number="Nano 3.0"]
  Q1 = MOSFET-NCHANNEL [part_number=BS170 package=to-92]
  Q4 = Basic FET P-Channel [part_number=50N06 package="TO220 [THT]"]
  D1 = Rectifier Diode [part_number=1N4001 package="300 mil [THT]"]
  D2 = Rectifier Diode [part_number=1N4001 package="300 mil [THT]"]
  D3 = Rectifier Diode [part_number=1N4001 package="300 mil [THT]"]
  D4 = Rectifier Diode [part_number=1N4001 package="300 mil [THT]"]
  D5 = Rectifier Diode [part_number=1N4001 package="300 mil [THT]"]
  BAT1 = BC9VPC [package=bc9vpc]
  IC1 = Voltage Regulator [part_number=7812 package=to-220-alt]
  C1 = Capacitor [part_number=100uF package=cap-pth-small2]
  C8 = Capacitor [part_number=100uF package=cap-pth-small2]
  R3 = Resistor [tolerance=±5% resistance=47k power=0.25W package=THT]
  THS = Temperature Sensor (Thermistor) [thermistor_type=NTC package=THT]
  R8 = Resistor [tolerance=±5% resistance=10 power=0.25W package=THT]
  R4 = Resistor [tolerance=±5% resistance=150k power=0.25W package=THT]
  Q4_2 = MOSFET-NCHANNEL [part_number=BS170 package=to-92]
  R9 = Resistor [tolerance=±5% resistance=1k power=0.25W package=THT]
  RV0 = TRIMPOT [part_number=20K package=trimpot_pth_s3_lock]
  JP3_3 = Header 2 [package=molex-1x2_lock]
  JP_I2C = Header 4 [package=molex-1x4_lock]
  JP_SRL = Header 4 [package=molex-1x4_lock]
  R10 = Resistor [tolerance=±5% resistance=100k power=0.25W package=THT]
  R11 = Resistor [tolerance=±1% resistance=1 power=3W package=THT]
  R12 = Resistor [tolerance=±1% resistance=1 power=3W package=THT]
  R13 = Resistor [tolerance=±1% resistance=1 power=3W package=THT]
  R14 = Resistor [tolerance=±1% resistance=1 power=3W package=THT]
  R15 = Resistor [tolerance=±1% resistance=1 power=3W package=THT]
  R16 = Resistor [tolerance=±1% resistance=1 power=3W package=THT]
  R17 = Resistor [tolerance=±1% resistance=1 power=3W package=THT]
  R18 = Resistor [tolerance=±1% resistance=1 power=3W package=THT]
  R19 = Resistor [tolerance=±1% resistance=1 power=3W package=THT]
  R20 = Resistor [tolerance=±1% resistance=1 power=3W package=THT]
  R11_2 = Resistor [tolerance=±5% resistance=470 power=0.25W package=THT]
  MOV1 = VA250LA40BP [part_number="50V MOV" package=VA250LA40BP]
  JP_PS = Header 2 [package=molex-1x2_lock]
  Q3 = Basic FET P-Channel [part_number=50N06 package="TO220 [THT]"]
  R8_2 = Resistor [tolerance=±5% resistance=470 power=0.25W package=THT]
  R7 = Resistor [tolerance=±5% resistance=1k power=0.25W package=THT]
  C5 = Capacitor [part_number=100uF package=cap-pth-small2]
  RV3 = TRIMPOT [part_number=10K package=trimpot_pth_s3_lock]
  R23 = Resistor [tolerance=±5% resistance=1k power=0.25W package=THT]
  R24 = Resistor [tolerance=±5% resistance=1k power=0.25W package=THT]
  FAN_LED = Header 2 [package=molex-1x2_lock]
  LED_PWR = Header 2 [package=molex-1x2_lock]
  OVER_C = Header 2 [package=molex-1x2_lock]
  Fuse1 = Fuse with Handler [part_number="Htc-15m - 700mA Fuse"]
  JP_PWR = Header 2 [package=molex-1x2_lock]
  C3 = Electrolytic Capacitor [capacitance=1μF package="100 mil [THT, electrolytic]"]
  LED_FAN = LED - 5mm [color="Red (633nm)" package="5 mm [THT]"]
  LED_OVR = LED - 5mm [color="Red (633nm)" package="5 mm [THT]"]
  LED_PWR_2 = LED - 5mm [color="Red (633nm)" package="5 mm [THT]"]
  C7 = Tantalum Capacitor [capacitance=100nF package="100 mil [THT, tantalum]"]
  C6 = Tantalum Capacitor [capacitance=100nF package="100 mil [THT, tantalum]"]
  TH1 = Header 2 [package=molex-1x2_lock]
  C12 = Electrolytic Capacitor [capacitance=100µF package="100 mil [THT, electrolytic]"]
  C4 = Electrolytic Capacitor [capacitance=100µF package="100 mil [THT, electrolytic]"]
  J1 = Dagu DGServo 9g header connector (female) [package=THT]  # not connected
  JQ3 = Header 3 [package=molex-1x3_lock]  # not connected
  JQ4 = Header 3 [package=molex-1x3_lock]  # not connected

nets:
  N1: U1.1OUT, Q4_2.G, OVER_C.1, LED_OVR.anode
  N2: U1.1IN-, U1.2IN-, THS.pin_1, R8.Pin_0, R4.Pin_0, TH1.1
  N3: U1.1IN+, R4.Pin_1, RV0.WIPER
  VCC: U1.VCC+, RV2.CW, Part1.VCC, Part2.VIN, D1.cathode, IC1.OUT, C1.1, R8.Pin_1, RV0.CW, JP_I2C.1, JP_SRL.1, R10.Pin_1, LED_PWR.1, C3.+, LED_PWR_2.anode, C12.+
  N4: U1.2IN+, RV2.WIPER, R3.Pin_0
  N5: U1.2OUT, Q1.G, R3.Pin_1, FAN_LED.1, LED_FAN.anode
  GND: U1.VCC-, RV2.CCW, F1.GND, Part1.GND, Part2.GND, Q1.D, D4.anode, D5.anode, IC1.GND, C8.1, THS.pin_0, Q4_2.D, R9.Pin_0, RV0.CCW, JP_I2C.2, JP_SRL.2, R11.Pin_1, R12.Pin_1, R13.Pin_1, R14.Pin_1, R15.Pin_1, R16.Pin_1, R17.Pin_1, R18.Pin_1, R19.Pin_1, R20.Pin_1, MOV1.P$1, JP_PS.2, RV3.CCW, R23.Pin_0, R24.Pin_0, C3.-, C7.-, C6.-, TH1.2, C12.-, C4.-
  N6: U1.4IN+, Q4_2.S, R10.Pin_0, RV3.WIPER, RV3.CW
  N7: U1.4IN-, R7.Pin_0, C5.2
  N8: U1.4OUT, R11_2.Pin_1, R8_2.Pin_1
  N9: F1.5V, Q1.S, D1.anode, C1.2
  N10: Part1.SDA, Part2.A4, JP_I2C.3
  N11: Part1.SCL, Part2.A5, JP_I2C.4
  N12: Part2.D1/TX, JP_SRL.3
  N13: Part2.D0/RX, JP_SRL.4
  N14: Part2.RESET, Part2.5V
  N15: Part2.AREF, JP3_3.1
  N16: Part2.3V3, JP3_3.2
  N17: Q4.gate, R11_2.Pin_0, C7.+
  N18: Q4.drain, MOV1.P$2, Q3.drain, R7.Pin_1, C5.1, Fuse1.Connector1
  N19: Q4.source, R11.Pin_0, R12.Pin_0, R13.Pin_0, R14.Pin_0, R15.Pin_0, R16.Pin_0, R17.Pin_0, R18.Pin_0, R19.Pin_0, R20.Pin_0, Q3.source
  N20: D2.cathode, D3.cathode, IC1.IN, C8.2, C4.+
  N21: D2.anode, D4.cathode, BAT1.V-, JP_PWR.1
  N22: D3.anode, D5.cathode, BAT1.V+, JP_PWR.2
  N23: R9.Pin_1, OVER_C.2, LED_OVR.cathode
  N24: JP_PS.1, Fuse1.Connector2
  N25: Q3.gate, R8_2.Pin_0, C6.+
  N26: R23.Pin_1, FAN_LED.2, LED_FAN.cathode
  N27: R24.Pin_1, LED_PWR.2, LED_PWR_2.cathode

custom parts:
  Fan - Ventilador: Ventilador de 2 pines, se encuentra comunmente en computadoras de escritorio
  LCD1602-I2C: A standard character display, usually with 2x16 characters. Comes in many colors with LCM1602 IIC attached.
  VA250LA40BP: Varistor (V18za2p with hole size increased to .042 and breadboard vuiew fixed up.)
